# Fritzing sketch Complete circuit (saved by Fritzing 0.9.3b)
circuit board: 10.1776cm x 5.36194cm
breadboards: 4

parts:
  J9 = Basic Force Sensing Resistor (FSR) [package=THT]
  J3 = Basic Force Sensing Resistor (FSR) [package=THT]
  J4 = Basic Force Sensing Resistor (FSR) [package=THT]
  J2 = Basic Force Sensing Resistor (FSR) [package=THT]
  J1 = Basic Force Sensing Resistor (FSR) [package=THT]
  J6 = Basic Force Sensing Resistor (FSR) [package=THT]
  J7 = Basic Force Sensing Resistor (FSR) [package=THT]
  J10 = Basic Force Sensing Resistor (FSR) [package=THT]
  J8 = Basic Force Sensing Resistor (FSR) [package=THT]
  J5 = Basic Force Sensing Resistor (FSR) [package=THT]
  R10 = Resistor [tolerance=±5% resistance=10k package=THT]
  R9 = Resistor [tolerance=±5% resistance=10k package=THT]
  R8 = Resistor [tolerance=±5% resistance=10k package=THT]
  R7 = Resistor [tolerance=±5% resistance=10k package=THT]
  R6 = Resistor [tolerance=±5% resistance=10k package=THT]
  R1 = Resistor [tolerance=±5% resistance=10k package=THT]
  R2 = Resistor [tolerance=±5% resistance=10k package=THT]
  R3 = Resistor [tolerance=±5% resistance=10k package=THT]
  R4 = Resistor [tolerance=±5% resistance=10k package=THT]
  R5 = Resistor [tolerance=±5% resistance=10k package=THT]
  J11 = Basic Force Sensing Resistor (FSR) [package=THT]
  J12 = Basic Force Sensing Resistor (FSR) [package=THT]
  RS1 = Resistor [tolerance=±5% resistance=10k package=THT]
  RS2 = Resistor [tolerance=±5% resistance=10k package=THT]
  Arduino_Mega_Shield = Arduino Mega 2560 (Rev3)
  LED = RGB LED (com. cathode, rgb) [package="5 mm [THT]"]
  R11 = Resistor [tolerance=±5% resistance=220 package=THT]
  R12 = Resistor [tolerance=±5% resistance=220 package=THT]
  R13 = Resistor [tolerance=±5% resistance=220 package=THT]
  FETR = Basic FET N-Channel [part_number=IRL1004PBF package="TO220 [THT]"]
  PD_RR = Resistor [tolerance=±5% resistance=10k package=THT]
  CR = Ceramic Capacitor [capacitance=10pF package="100 mil [THT, multilayer]"]
  DR = Rectifier Diode [part_number=1N4001 package="300 mil [THT]"]
  FETL = Basic FET N-Channel [part_number=IRL1004PBF package="TO220 [THT]"]
  PD_RL = Resistor [tolerance=±5% resistance=10k package=THT]
  CL = Ceramic Capacitor [capacitance=10pF package="100 mil [THT, multilayer]"]
  DL = Rectifier Diode [part_number=1N4001 package="300 mil [THT]"]
  VPM2_1 = Vibration Motor- ROB-08449 [package=vibe-motor-10mm]
  VPM2_2 = Vibration Motor- ROB-08449 [package=vibe-motor-10mm]
  MPU-6050 = MPU-6050 Board GY-521 [form="♀ (female)" package=THT]

nets:
  N1: J9.pin_0, R9.Pin_0, Arduino_Mega_Shield.A1
  N2: J9.pin_1, J3.pin_1, J4.pin_1, J2.pin_1, J1.pin_1, J6.pin_1, J7.pin_1, J10.pin_1, J8.pin_1, J5.pin_1, J11.pin_1, J12.pin_1, Arduino_Mega_Shield.5V, CR.1, DR.cathode, CL.1, DL.cathode, VPM2_1.+, VPM2_2.+, MPU-6050.pin1
  N3: J3.pin_0, R3.Pin_0, Arduino_Mega_Shield.A7
  N4: J4.pin_0, R4.Pin_0, Arduino_Mega_Shield.A6
  N5: J2.pin_0, R2.Pin_0, Arduino_Mega_Shield.A8
  N6: J1.pin_0, R1.Pin_0, Arduino_Mega_Shield.A9
  N7: J6.pin_0, R6.Pin_0, Arduino_Mega_Shield.A4
  N8: J7.pin_0, R7.Pin_0, Arduino_Mega_Shield.A3
  N9: J10.pin_0, R10.Pin_0, Arduino_Mega_Shield.A0
  N10: J8.pin_0, R8.Pin_0, Arduino_Mega_Shield.A2
  N11: J5.pin_0, R5.Pin_0, Arduino_Mega_Shield.A5
  N12: R10.Pin_1, R9.Pin_1, R8.Pin_1, R7.Pin_1, R6.Pin_1, R1.Pin_1, R2.Pin_1, R3.Pin_1, R4.Pin_1, R5.Pin_1, RS1.Pin_1, RS2.Pin_1, Arduino_Mega_Shield.GND, LED.common_cathode, FETR.source, PD_RR.Pin_1, FETL.source, PD_RL.Pin_1, MPU-6050.pin2
  N13: J11.pin_0, RS1.Pin_0, Arduino_Mega_Shield.A10
  N14: J12.pin_0, RS2.Pin_0, Arduino_Mega_Shield.A11
  N15: Arduino_Mega_Shield.D21/SCL, MPU-6050.pin3
  N16: Arduino_Mega_Shield.D20/SDA, Arduino_Mega_Shield.SDA, MPU-6050.pin4
  N17: Arduino_Mega_Shield.D13_PWM, FETL.gate, PD_RL.Pin_0
  N18: Arduino_Mega_Shield.D12_PWM, FETR.gate, PD_RR.Pin_0
  N19: Arduino_Mega_Shield.D2_PWM, MPU-6050.pin8
  N20: Arduino_Mega_Shield.D4_PWM, R11.Pin_0
  N21: Arduino_Mega_Shield.D5_PWM, R13.Pin_0
  N22: Arduino_Mega_Shield.D6_PWM, R12.Pin_0
  N23: LED.red_anode, R12.Pin_1
  N24: LED.green_anode, R13.Pin_1
  N25: LED.blue_anode, R11.Pin_1
  N26: FETR.drain, CR.0, DR.anode, VPM2_2.-
  N27: FETL.drain, CL.0, DL.anode, VPM2_1.-

notes:
  Diyar Gur - 10.2019
  EFFENDI Arduino Mega Shield

custom parts:
  Vibration Motor- ROB-08449: Vibration Motor- ROB-08449 Physical dimension and wire connections for this powerful vibration motor. Motor has a self adhesive backing.
  MPU-6050 Board GY-521: Acelerometro y Giroscopio MPU-6050 Board GY-521
